# Fritzing sketch timer-ruler_v4_inkl_Values (saved by Fritzing 0.9.2b)
circuit board: 3.3cm x 3.3cm
breadboards: 1

parts:
  R1 = Resistor [tolerance=±5% resistance=68 package="0805 [SMD]"]
  R2 = Resistor [tolerance=±5% resistance=68 package="0805 [SMD]"]
  R3 = Resistor [tolerance=±5% resistance=68 package="0805 [SMD]"]
  R4 = Resistor [tolerance=±5% resistance=68 package="0805 [SMD]"]
  R5 = Resistor [tolerance=±5% resistance=68 package="0805 [SMD]"]
  R6 = Resistor [tolerance=±5% resistance=47 package="0805 [SMD]"]
  R7 = Resistor [tolerance=±5% resistance=47 package="0805 [SMD]"]
  R8 = Resistor [tolerance=±5% resistance=47 package="0805 [SMD]"]
  R9 = Resistor [tolerance=±5% resistance=47 package="0805 [SMD]"]
  1 = smd LED [color="Red (660nm)" part_number="SMD LED 0805 Rot 100 mcd 120Grad 20 mA 1.85 V Kingbright KP-2012SRC-PRV" package="0805 [SMD]"]
  2 = smd LED [color="Red (660nm)" part_number="SMD LED 0805 Rot 100 mcd 120Grad 20 mA 1.85 V Kingbright KP-2012SRC-PRV" package="0805 [SMD]"]
  3 = smd LED [color="Red (660nm)" part_number="SMD LED 0805 Rot 100 mcd 120Grad 20 mA 1.85 V Kingbright KP-2012SRC-PRV" package="0805 [SMD]"]
  4 = smd LED [color="Red (660nm)" part_number="SMD LED 0805 Rot 100 mcd 120Grad 20 mA 1.85 V Kingbright KP-2012SRC-PRV" package="0805 [SMD]"]
  5 = smd LED [color="Red (660nm)" part_number="SMD LED 0805 Rot 100 mcd 120Grad 20 mA 1.85 V Kingbright KP-2012SRC-PRV" package="0805 [SMD]"]
  6 = smd LED [color="Orange (605nm)" part_number="SMD LED 0805 Orange 180 mcd 120Grad 20 mA 2.1 V Kingbright KP-2012SECK" package="0805 [SMD]"]
  7 = smd LED [color="Orange (605nm)" part_number="SMD LED 0805 Orange 180 mcd 120Grad 20 mA 2.1 V Kingbright KP-2012SECK" package="0805 [SMD]"]
  8 = smd LED [color="Orange (605nm)" part_number="SMD LED 0805 Orange 180 mcd 120Grad 20 mA 2.1 V Kingbright KP-2012SECK" package="0805 [SMD]"]
  9 = smd LED [color="Green (570nm)" part_number="SMD LED 0805 Grün 50 mcd 120Grad 20 mA 2.1 V Kingbright KP-2012CGCK" package="0805 [SMD]"]
  T2 = Momentary Switch [package=tactile_switch_smd]
  T3 = Momentary Switch [package=tactile_switch_smd]
  R10 = Resistor [tolerance=±5% resistance=10k package="0805 [SMD]"]
  8MHz = OSCILLATOR [part_number="SMD-Quarz MQ-Serie Keramik EuroQuartz 8.000MHZ MQ 30/30/40/12PF Frequenz 8.000000 MHz (L x B x H) 7 x 5 x 1.2 mm, " package=crystal-smd-7x5]
  C1 = Ceramic Capacitor [capacitance=22pF package="0805 [SMD, multilayer]"]
  C2 = Ceramic Capacitor [capacitance=22pF package="0805 [SMD, multilayer]"]
  ISP = AVR ISP 6 Pin [package=2x3]
  BAT1 = Battery Holders [part_number="CR2032, Knopfzellenhalter 1 CR 2032 Horizontal, Oberflächenmontage SMD (L x B x H) 30.7 x 20 x 4 mm Renata 100340" package=battcon_20mm]
  RST = Momentary Switch [package=tactile_switch_smd]
  S8 = SPST Switch [package=switch-spdt-smd]
  JP1 = Header 2 [package=molex-1x2_lock]
  T1 = Momentary Switch [package=tactile_switch_smd]
  Atmega328 = ATmega328 [package=tqfp]

nets:
  N1: R1.Pin_0, Atmega328.PD0(RXD)
  N2: R1.Pin_1, 1.anode
  N3: R2.Pin_0, Atmega328.PD1(TXD)
  N4: R2.Pin_1, 2.anode
  N5: R3.Pin_0, Atmega328.PD2(INT0)
  N6: R3.Pin_1, 3.anode
  N7: R4.Pin_0, Atmega328.PD3(INT1)
  N8: R4.Pin_1, 4.anode
  N9: R5.Pin_0, Atmega328.PD4(XCK_T0)
  N10: R5.Pin_1, 5.anode
  N11: R6.Pin_0, Atmega328.PD5(T1)
  N12: R6.Pin_1, 6.anode
  N13: R7.Pin_0, Atmega328.PD6(AIN0)
  N14: R7.Pin_1, 7.anode
  N15: R8.Pin_0, Atmega328.PD7(AIN1)
  N16: R8.Pin_1, 8.anode
  N17: R9.Pin_0, Atmega328.PB1(OC1A)
  N18: R9.Pin_1, 9.anode
  GND: 1.cathode, 2.cathode, 3.cathode, 4.cathode, 5.cathode, 6.cathode, 7.cathode, 8.cathode, 9.cathode, T2.1, T3.1, C1.0, C2.0, ISP.6, BAT1.-_, RST.1, T1.1, Atmega328.GND, Atmega328.AGND
  N19: T2.3, Atmega328.PC1(ADC1)
  N20: T3.3, Atmega328.PC2(ADC2)
  5V: R10.Pin_0, ISP.2, S8.P, Atmega328.VCC, Atmega328.AVCC
  N21: R10.Pin_1, ISP.5, RST.3, Atmega328.PC6(_RESET)
  N22: 8MHz.EN, C2.1, Atmega328.PB7(XTAL2_TOSC2)
  N23: 8MHz.OUT, C1.1, Atmega328.PB6(XTAL1_TOSC1)
  N24: ISP.1, Atmega328.PB4(MISO)
  N25: ISP.3, Atmega328.PB5(SCK)
  N26: ISP.4, Atmega328.PB3(MOSI_OC2)
  N27: BAT1.+_, S8.S
  N28: JP1.1, Atmega328.PC5(ADC5_SCL)
  N29: JP1.2, Atmega328.PC4(ADC4_SDA)
  N30: T1.3, Atmega328.PC0(ADC0)

notes:
  sda
  scl
  rote LED: SMD LED 0805 Rot 100 mcd 120Grad 20 mA 1.85 V Kingbright KP-2012SRC-PRV -> 68 Ohm
  orange LED: SMD LED 0805 Orange 180 mcd 120Grad 20 mA 2.1 V Kingbright KP-2012SECK -> 47 Ohm
  grün LED: SMD LED 0805 Grün 50 mcd 120Grad 20 mA 2.1 V Kingbright KP-2012CGCK -> 47 Ohm

custom parts:
  OSCILLATOR: Generic 5x3 and 7x5 oscillators
  Battery Holders: Battery Holders Various common sizes : AA, AAA, 20mm coin cell and 12mm coin cell.
